// Logisim project Logisim.circ as structural Verilog: 5 circuits, main circuit main
module main (
  input  [7:0] in_1,
  input  [7:0] in_2,
  input  [7:0] in_3,
  input  [7:0] in_4,
  input  [7:0] in_5,
  input  [7:0] in_6,
  input  [7:0] in_7,
  input  [7:0] in_8,
  input  [7:0] in_9,
  input  [7:0] in_10,
  input  [7:0] in_11,
  input  [7:0] in_12,
  input  [7:0] in_13,
  input  [7:0] in_14,
  input  [7:0] in_15,
  input  [7:0] in_16,
  input  [7:0] in_17,
  input  [7:0] in_18,
  input  [7:0] in_19,
  input  [7:0] in_20,
  input  [4:0] in_21,
  input  [7:0] in_22,
  input  [7:0] in_23,
  input  [7:0] in_24,
  input  [7:0] in_25,
  input  [7:0] in_26,
  input  [7:0] in_27,
  input  [7:0] in_28,
  input  [7:0] in_29,
  input  [7:0] in_30,
  input  [7:0] in_31,
  input  [7:0] in_32,
  input  [7:0] in_33,
  output [63:0] out_34
);

  wire [63:8] undriven, undriven_2, undriven_3, undriven_4, undriven_5, undriven_6, undriven_7, undriven_8,
       undriven_9, undriven_10, undriven_11, undriven_12, undriven_13, undriven_14, undriven_15, undriven_16,
       undriven_17, undriven_18, undriven_19, undriven_20, undriven_21, undriven_22, undriven_23,
       undriven_24, undriven_25, undriven_26, undriven_27, undriven_28;

  Multiplexer #(.enable("false"), .select(5), .width(64)) multiplexer_1 (
    .in0({undriven_28, in_1}), .in1({undriven_15, in_2}), .in2({undriven_19, in_3}),
    .in3({undriven_23, in_4}), .in4({undriven_6, in_5}), .in5({undriven_2, in_6}), .in6({undriven_3, in_12}),
    .in7({undriven_7, in_13}), .in8({undriven_10, in_7}), .in9({undriven_14, in_8}),
    .in10({undriven_20, in_9}), .in11({undriven_24, in_10}), .in12({undriven_27, in_11}),
    .in13({undriven, in_20}), .in14({undriven_5, in_19}), .in15({undriven_9, in_14}),
    .in16({undriven_12, in_15}), .in17({undriven_17, in_16}), .in18({undriven_22, in_17}),
    .in19({undriven_26, in_18}), .in20({undriven_27, in_11}), .in21({undriven_4, in_27}),
    .in22({undriven_8, in_22}), .in23({undriven_11, in_25}), .in24({undriven_16, in_23}),
    .in25({undriven_21, in_24}), .in26({undriven_25, in_26}), .in27({undriven, in_20}),
    .in28({undriven_5, in_19}), .in29({undriven_9, in_14}), .in30({undriven_13, in_31}),
    .in31({undriven_18, in_30}), .out(out_34), .sel(in_21));
  // Pins of 8 and 64 bits meet at {undriven_27, in_11}
  // Pins of 8 and 64 bits meet at {undriven, in_20}
  // Pins of 8 and 64 bits meet at {undriven_2, in_6}
  // Pins of 8 and 64 bits meet at {undriven_3, in_12}
  // Pins of 8 and 64 bits meet at {undriven_4, in_27}
  // Pins of 8 and 64 bits meet at {undriven_5, in_19}
  // Pins of 8 and 64 bits meet at {undriven_6, in_5}
  // Pins of 8 and 64 bits meet at {undriven_7, in_13}
  // Pins of 8 and 64 bits meet at {undriven_8, in_22}
  // Pins of 8 and 64 bits meet at {undriven_9, in_14}
  // Pins of 8 and 64 bits meet at {undriven_10, in_7}
  // Pins of 8 and 64 bits meet at {undriven_11, in_25}

  assign in_28 = in_11;
  assign in_29 = in_14;
  assign in_32 = in_19;
  assign in_33 = in_20;
endmodule

module HalfAdder (
  input  In1,
  input  In2,
  output Carry,
  output Out1
);

  wire or_1_out;

  or or_1 (or_1_out, In1, In2);
  and and_1 (Carry, In2, In1);
  xor xor_1 (Out1, Carry, or_1_out);
endmodule

module FullAdder (
  input  In1,
  input  In2,
  input  CarryIn,
  output Carry,
  output Result
);

  wire and_1_out, halfadder_1_carry, halfadder_1_out1;

  HalfAdder halfadder_1 (.Carry(halfadder_1_carry), .Out1(halfadder_1_out1), .In1(In1), .In2(In2));
  xor xor_1 (Result, CarryIn, halfadder_1_out1);
  or or_1 (Carry, halfadder_1_carry, and_1_out);
  and and_1 (and_1_out, halfadder_1_out1, CarryIn);
endmodule

module EightBitAdder (
  input  CarryIn,
  input  [7:0] in_2,
  input  [7:0] in_3,
  output [7:0] out_4,
  output CarryOut
);

  wire fulladder_1_carry, fulladder_2_carry, fulladder_3_carry, fulladder_4_carry, fulladder_5_carry,
       fulladder_6_carry, fulladder_7_carry;

  FullAdder fulladder_1 (.In1(in_2[0]), .In2(in_3[0]), .CarryIn(CarryIn), .Carry(fulladder_1_carry), .Result(out_4[0]));
  FullAdder fulladder_2 (
    .In1(in_2[1]), .In2(in_3[1]), .CarryIn(fulladder_1_carry), .Carry(fulladder_2_carry), .Result(out_4[1]));
  FullAdder fulladder_3 (
    .In1(in_2[2]), .In2(in_3[2]), .CarryIn(fulladder_2_carry), .Carry(fulladder_3_carry), .Result(out_4[2]));
  FullAdder fulladder_4 (
    .In1(in_2[3]), .In2(in_3[3]), .CarryIn(fulladder_3_carry), .Carry(fulladder_4_carry), .Result(out_4[3]));
  FullAdder fulladder_5 (
    .In1(in_2[4]), .In2(in_3[4]), .CarryIn(fulladder_4_carry), .Carry(fulladder_5_carry), .Result(out_4[4]));
  FullAdder fulladder_6 (
    .In1(in_2[5]), .In2(in_3[5]), .CarryIn(fulladder_5_carry), .Carry(fulladder_6_carry), .Result(out_4[5]));
  FullAdder fulladder_7 (
    .In1(in_2[6]), .In2(in_3[6]), .CarryIn(fulladder_6_carry), .Carry(fulladder_7_carry), .Result(out_4[6]));
  FullAdder fulladder_8 (
    .In1(in_2[7]), .In2(in_3[7]), .CarryIn(fulladder_7_carry), .Carry(CarryOut), .Result(out_4[7]));
endmodule

module LogicGateDeriving (
  input  in_1,
  input  in_2,
  input  in_3,
  input  in_4,
  input  in_5,
  input  in_6,
  input  in_7,
  input  in_8,
  input  in_9,
  input  in_10,
  input  in_11,
  input  in_12,
  input  in_13,
  output out_14,
  output out_15,
  output out_16,
  output out_17,
  output out_18,
  output out_19,
  output out_20
);

  wire nand_2_out, nand_3_out, nand_4_out, nand_5_out, not_3_out, not_5_out, not_6_out, or_1_out, or_2_out,
       xor_1_out;

  or or_1 (or_1_out, in_8, in_9);
  nand nand_1 (out_14, in_1, in_1);
  nand nand_2 (nand_2_out, in_2, in_3);
  nand nand_3 (nand_3_out, in_4, in_6);
  not not_1 (out_18, or_1_out);
  nand nand_4 (nand_4_out, in_10, in_11);
  or or_2 (or_2_out, in_10, in_11);
  xor xor_1 (xor_1_out, in_12, in_13);
  not not_2 (out_15, nand_2_out);
  not not_3 (not_3_out, in_4);
  nand nand_5 (nand_5_out, nand_3_out, in_6);
  not not_4 (out_20, xor_1_out);
  and and_1 (out_19, nand_4_out, or_2_out);
  nand nand_6 (out_16, not_3_out, nand_5_out);
  not not_5 (not_5_out, in_5);
  not not_6 (not_6_out, in_7);
  nand nand_7 (out_17, not_5_out, not_6_out);
endmodule
